# Fritzing sketch arduino_breadboard (saved by Fritzing 0.9.3b)
breadboards: 1

parts:
  ArduinoNano = Arduino Nano (Rev3.0) (ICSP)
  LED = LED - 5mm [color="Red (633nm)" package="5 mm [THT]"]
  LDR = Photocell (LDR) [package=THT]
  R2 = Resistor [tolerance=±5% resistance=220 package="0805 [SMD]"]
  R2_2 = Resistor [tolerance=±5% resistance=220 package="0603 [SMD]"]

nets:
  N1: ArduinoNano.GND, R2.Pin_0, R2_2.Pin_0
  N2: ArduinoNano.D3, LED.anode
  N3: ArduinoNano.5V, LDR.pin_1
  N4: ArduinoNano.A0, LDR.pin_0, R2.Pin_1
  N5: LED.cathode, R2_2.Pin_1
